# Fritzing sketch raspi-arduino-mega (saved by Fritzing 0.9.3b)
breadboards: 2

parts:
  Part1 = Arduino Mega 2560 (Rev3)
  J1 = Piezo Speaker
  U1 = 74HC595 [package="DIP16 [THT]"]
  DI1 = 7-Segment LED Display [package=THT]
  R1 = Resistor [tolerance=±5% resistance=220 package=THT]
  LED1 = RGB LED - (4 legs) [package="5 mm [THT]"]
  R2 = Resistor [tolerance=±5% resistance=220 package=THT]
  R3 = Resistor [tolerance=±5% resistance=220 package=THT]
  R4 = Resistor [tolerance=±5% resistance=220 package=THT]

nets (from the breadboard view):
  GND: Part1.GND, J1.pin1, U1.GND, U1.OE, R1.Pin_1
  5V: Part1.5V, U1.MR, U1.VCC, LED1.common_anode
  N1: Part1.D4_PWM, R2.Pin_0
  N2: Part1.D5_PWM, R3.Pin_0
  N3: Part1.D6_PWM, R4.Pin_0
  N4: Part1.D7_PWM, J1.pin2
  N5: Part1.D31, U1.DS
  N6: Part1.D32, U1.ST_CP
  N7: Part1.D33, U1.SH_CP
  N8: U1.Q1, DI1.cathodeB
  N9: U1.Q2, DI1.cathodeC
  N10: U1.Q3, DI1.cathodeD
  N11: U1.Q4, DI1.cathodeE
  N12: U1.Q5, DI1.cathodeF
  N13: U1.Q6, DI1.cathodeG
  N14: U1.Q7, DI1.cathodeDP
  N15: U1.Q0, DI1.cathodeA
  N16: DI1.commAnode#7, R1.Pin_0
  N17: LED1.red_cathode, R2.Pin_1
  N18: LED1.green_cathode, R3.Pin_1
  N19: LED1.blue_cathode, R4.Pin_1
