# Fritzing sketch raspi-arduino-uno (saved by Fritzing 0.9.3b)

parts:
  Arduino_UNO = Arduino Uno (Rev3)
  L298N = L298_BRIDGE_DRIVER [package=powerso20]
  M1 = DC Motor
  M2 = DC Motor
  M3 = DC Motor
  hc-sr1 = hc-sr04 [part_number=RIGHT]
  hc-sr2 = hc-sr04 [part_number=LEFT]
  S1 = Toggle Switch [package=THT]
  U1 = LIPO-2000mAh [package=lipo-2000]
  M4 = DC Motor

nets:
  N1: Arduino_UNO.D8, L298N.IN3
  N2: Arduino_UNO.D9_PWM, L298N.IN2
  N3: Arduino_UNO.D10_PWM/SS, L298N.IN1
  N4: Arduino_UNO.D11_PWM/MOSI, hc-sr1.Trig, hc-sr1.Echo
  N5: Arduino_UNO.D3_PWM, hc-sr2.Trig, hc-sr2.Echo
  N6: Arduino_UNO.D5_PWM, L298N.ENB
  N7: Arduino_UNO.D6_PWM, L298N.ENA
  N8: Arduino_UNO.D7, L298N.IN4
  VCC: Arduino_UNO.5V, hc-sr1.VCC, hc-sr2.VCC
  GND: Arduino_UNO.GND, hc-sr1.GND, hc-sr2.GND
  N9: L298N.GND, S1.L1, U1.-
  N10: L298N.OUT1, M2.pin_1, M3.pin_1
  N11: L298N.OUT2, M2.pin_2, M3.pin_2
  N12: L298N.VSS, S1.L2
  N13: L298N.OUT3, M1.pin_1, M4.pin_1
  N14: L298N.OUT4, M1.pin_2, M4.pin_2
  N15: S1.COM, U1.+
